# Fritzing sketch diagrama_esquematico (saved by Fritzing 0.9.2b)

parts:
  microSD_Transflash1 = SparkFun - microSD Transflash
  Componente2 = Arduino Nano (Rev3.0)
  S2 = Momentary Switch [package=tactile-pth]
  LED1 = LED - 3mm [color="Red (633nm)" package="3 mm [THT]"]
  LED2 = LED - 3mm [color="Green (565nm)" package="3 mm [THT]"]
  R1 = Resistor [tolerance=±5% resistance=220 package=THT]
  R2 = Resistor [tolerance=±5% resistance=220 package=THT]
  J1 = Screw terminal - 2 pins [package=THT]
  J2 = Screw terminal - 2 pins [package=THT]
  J3 = Screw terminal - 2 pins [package=THT]
  J4 = Screw terminal - 2 pins [package=THT]
  R3 = Resistor [tolerance=±5% resistance=220 package=THT]

nets:
  N1: microSD_Transflash1.DO, Componente2.D12/MISO
  GND: microSD_Transflash1.GND, Componente2.GND, LED1.cathode, LED2.cathode, R1.Pin_0, J3.pin2, J4.pin2
  N2: microSD_Transflash1.SCK, Componente2.D13/SCK
  VCC: microSD_Transflash1.VCC, Componente2.5V, S2.2, J4.pin1
  N3: microSD_Transflash1.DI, Componente2.D11/MOSI
  N4: microSD_Transflash1.CS, Componente2.D9
  N5: Componente2.D2, R3.Pin_0
  N6: Componente2.D3, J3.pin1
  N7: Componente2.D4, R2.Pin_0
  N8: Componente2.D5, S2.1, R1.Pin_1
  N9: Componente2.A4, J1.pin1
  N10: Componente2.A3, J1.pin2
  N11: Componente2.A2, J2.pin1
  N12: Componente2.A1, J2.pin2
  N13: LED1.anode, R2.Pin_1
  N14: LED2.anode, R3.Pin_1
